# Fritzing sketch LED02 (saved by Fritzing 0.9.3b)
breadboards: 1

parts:
  U1 = NodeMCU V1.0
  R1 = Rotary Potentiometer (Small) [maximum_resistance=100kΩ package=THT]

nets:
  N1: U1.3V3, R1.leg1
  N2: U1.GND, R1.leg2
  N3: U1.A0, R1.wiper

custom parts:
  NodeMCU V1.0: ESP8266 based NodeMCU
