# Fritzing sketch LED03 (saved by Fritzing 0.9.3b)
breadboards: 1

parts:
  U1 = NodeMCU V1.0
  R2 = Resistor [tolerance=±5% resistance=220 package=THT]
  R3 = Rotary Potentiometer (Small) [maximum_resistance=100kΩ package=THT]
  LED1 = LED - 5mm [color="Red (633nm)" package="5 mm [THT]"]

nets:
  N1: U1.D1, LED1.anode
  N2: U1.3V3, R3.leg1
  N3: U1.GND, R2.Pin_0, R3.leg2
  N4: U1.A0, R3.wiper
  N5: R2.Pin_1, LED1.cathode

custom parts:
  NodeMCU V1.0: ESP8266 based NodeMCU
